# Fritzing sketch temperature_sensor (saved by Fritzing 0.9.3b)
circuit board: 9.5cm x 6cm
breadboards: 2

parts:
  Part1 = Adafruit Feather HUZZAH ESP8266 [part_number="Adafruit #2821"]
  Part2 = SHARP Memory Display 1.3 inch 96x96 [part_number=3502]
  DHT1 = DHT11 Humitidy and Temperature Sensor
  R1 = Resistor [tolerance=±5% resistance=10k package="0805 [SMD]"]

nets:
  GND: Part1.GND, Part2.GND, DHT1.GND
  3.3V: Part1.3.3V, Part2.3.3V, DHT1.VDD, R1.Pin_0
  N1: Part1.GPIO0, DHT1.DATA, R1.Pin_1
  N2: Part1.GPIO16, Part2.CS
  N3: Part1.GPIO2, Part2.MOSI
  N4: Part1.GPIO5/SCL, Part2.SCLK

custom parts:
  Adafruit Feather HUZZAH ESP8266: his is the Adafruit Feather HUZZAH ESP8266 - our take on an 'all-in-one' ESP8266 WiFi development board with built in USB and battery charging. Its an ESP8266 WiFi module with all the extras you need, ready to rock! We have other boards in the Feather family, check'em out here. At the Feather HUZZAH's heart is an ESP8266 WiFi microcontroller clocked at 80 MHz and at 3.3V logic. This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
  SHARP Memory Display 1.3 inch 96x96: The 1.3" SHARP Memory LCD display is a cross between an eInk (e-paper) display and an LCD. It has the ultra-low power usage of eInk and the fast-refresh rates of an LCD. This model has a matt silver background, and pixels show up as little mirrors for a silver-reflective display, a really beautiful and unique look. It does not have a backlight, but it is daylight readable. For dark/night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
  DHT11 Humitidy and Temperature Sensor: DHT11 Humidity and Temperature Sensor
